// Digital circuit antikythera.dig as structural Verilog
module antikythera (
);

  wire and_2_out, comparator_1_eq, demultiplexer_1_out_0, demultiplexer_1_out_1, demultiplexer_1_out_2,
       demultiplexer_1_out_3, not_1_out, not_2_out, or_1_out, or_2_out, or_3_out, or_4_out, or_6_out,
       undriven, undriven_4, undriven_5, undriven_6;
  wire [1:0] multiplexer_14_out;
  wire [3:0] FR_q;
  wire [3:1] add_and_compare_1_c;
  wire [7:0] A_2_q, A_q, add_and_compare_1_s, and_1_out, AR_q, B_q, c__addr_q, demultiplexer_2_out_0,
       demultiplexer_2_out_1, demultiplexer_2_out_2, demultiplexer_2_out_3, IP_out, IR0_q, IR1_q, IR2_q,
       lower_d, multiplexer_1_out, multiplexer_2_out, multiplexer_3_out, multiplexer_4_out,
       multiplexer_5_out, multiplexer_6_out, multiplexer_7_out, multiplexer_8_out, multiplexer_9_out,
       multiplexer_10_out, multiplexer_11_out, multiplexer_12_out, multiplexer_13_out, multiplexer_15_out,
       multiplexer_16_out, multiplexer_17_out, or_5_out, ramdualport_1_d, ramdualport_2_d, ramdualport_3_d,
       ramdualport_4_d, register_1_q, register_2_q, register_3_q, register_4_q, rom_1_d, rom_1_d_2,
       rom_1_d_3, rom_1_d_4, RR_q, TR_q, undriven_7, upper_d, X_q, xor_1_out, xor_2_out;
  wire [7:1] undriven_2;
  wire [7:7] undriven_3;

  Multiplexer #(.Selector_Bits(2), .Bits(8)) multiplexer_1 (
    .in_0(register_4_q), .in_1(register_3_q), .in_2(register_2_q), .in_3(register_1_q),
    .out(multiplexer_1_out));  // open: sel
  Register #(.Bits(8)) c__addr (.D(undriven_7), .Q(c__addr_q));  // open: C, en
  RAMDualPort #(.Bits(8)) ramdualport_1 (
    .A(undriven_7[5:4]), .Din(register_4_q), .str(1'b0), .C(1'b0), .ld(1'b0), .D(ramdualport_1_d));
  RAMDualPort #(.Bits(8)) ramdualport_2 (
    .A(undriven_7[5:4]), .Din(register_3_q), .str(1'b0), .C(1'b0), .ld(1'b0), .D(ramdualport_2_d));
  RAMDualPort #(.Bits(8)) ramdualport_3 (
    .A(undriven_7[5:4]), .Din(register_2_q), .str(1'b0), .C(1'b0), .ld(1'b0), .D(ramdualport_3_d));
  RAMDualPort #(.Bits(8)) ramdualport_4 (
    .A(undriven_7[5:4]), .Din(register_1_q), .str(1'b0), .C(1'b0), .ld(1'b0), .D(ramdualport_4_d));
  ROM #(.AddrBits(5), .Bits(32)) rom_1 (
    .A(undriven_7[5:1]), .sel(1'b1), .D({rom_1_d_4, rom_1_d_3, rom_1_d_2, rom_1_d}));
  Comparator #(.Bits(8)) comparator_1 (.a(c__addr_q), .b(undriven_7), .eq(comparator_1_eq));  // open: gt, lt
  Register #(.Bits(8)) register_1 (.D(multiplexer_2_out), .C(undriven_6), .en(or_1_out), .Q(register_1_q));
  Register #(.Bits(8)) register_2 (.D(multiplexer_3_out), .C(undriven_6), .en(or_2_out), .Q(register_2_q));
  Register #(.Bits(8)) register_3 (.D(multiplexer_4_out), .C(undriven_6), .en(or_3_out), .Q(register_3_q));
  Register #(.Bits(8)) register_4 (.D(multiplexer_5_out), .C(undriven_6), .en(or_4_out), .Q(register_4_q));
  Multiplexer #(.Bits(8)) multiplexer_2 (
    .sel(undriven_5), .in_0(demultiplexer_2_out_3), .in_1(multiplexer_9_out), .out(multiplexer_2_out));
  Multiplexer #(.Bits(8)) multiplexer_3 (
    .sel(undriven_5), .in_0(demultiplexer_2_out_2), .in_1(multiplexer_8_out), .out(multiplexer_3_out));
  Multiplexer #(.Bits(8)) multiplexer_4 (
    .sel(undriven_5), .in_0(demultiplexer_2_out_1), .in_1(multiplexer_7_out), .out(multiplexer_4_out));
  Multiplexer #(.Bits(8)) multiplexer_5 (
    .sel(undriven_5), .in_0(demultiplexer_2_out_0), .in_1(multiplexer_6_out), .out(multiplexer_5_out));
  Multiplexer #(.Bits(8)) multiplexer_6 (
    .sel(undriven_7[0]), .in_0(ramdualport_1_d), .in_1(rom_1_d), .out(multiplexer_6_out));
  Multiplexer #(.Bits(8)) multiplexer_7 (
    .sel(undriven_7[0]), .in_0(ramdualport_2_d), .in_1(rom_1_d_2), .out(multiplexer_7_out));
  Multiplexer #(.Bits(8)) multiplexer_8 (
    .sel(undriven_7[0]), .in_0(ramdualport_3_d), .in_1(rom_1_d_3), .out(multiplexer_8_out));
  Multiplexer #(.Bits(8)) multiplexer_9 (
    .sel(undriven_7[0]), .in_0(ramdualport_4_d), .in_1(rom_1_d_4), .out(multiplexer_9_out));
  or or_1 (or_1_out, demultiplexer_1_out_3, undriven_4);
  or or_2 (or_2_out, demultiplexer_1_out_2, undriven_4);
  or or_3 (or_3_out, demultiplexer_1_out_1, undriven_4);
  or or_4 (or_4_out, demultiplexer_1_out_0, undriven_4);
  Demultiplexer #(.Selector_Bits(2)) demultiplexer_1 (
    .in(1'b0), .out_0(demultiplexer_1_out_0), .out_1(demultiplexer_1_out_1), .out_2(demultiplexer_1_out_2),
    .out_3(demultiplexer_1_out_3));  // open: sel
  Demultiplexer #(.Selector_Bits(2)) demultiplexer_2 (
    .in(1'b0), .out_0(demultiplexer_2_out_0[0]), .out_1(demultiplexer_2_out_1[0]),
    .out_2(demultiplexer_2_out_2[0]), .out_3(demultiplexer_2_out_3[0]));  // open: sel
  // Not not_1 has open pins: in=open, out=not_1_out
  CounterPreset #(.Bits(8)) IP (
    .en(not_1_out), .C(undriven), .dir(1'b0), .in(multiplexer_17_out), .clr(1'b0), .out(IP_out));  // open: ld, ovf
  Register #(.Bits(8)) RR (.D(IP_out), .C(undriven), .Q(RR_q));  // open: en
  Register #(.Bits(8)) AR (.D(multiplexer_15_out), .C(undriven), .Q(AR_q));  // open: en
  Register #(.Bits(8)) IR0 (.D(multiplexer_15_out), .C(undriven), .en(1'b1), .Q(IR0_q));
  Multiplexer #(.Selector_Bits(2), .Bits(8)) multiplexer_10 (
    .in_0(A_2_q), .in_1(X_q), .in_2(RR_q), .in_3(multiplexer_15_out), .out(multiplexer_10_out));  // open: sel
  Multiplexer #(.Selector_Bits(2), .Bits(8)) multiplexer_11 (
    .in_0(A_2_q), .in_1(X_q), .in_2(IP_out), .in_3(multiplexer_15_out), .out(multiplexer_11_out));  // open: sel
  Multiplexer #(.Selector_Bits(2), .Bits(8)) multiplexer_12 (
    .in_0(A_2_q), .in_1(X_q), .in_2({undriven_2, 1'b0}), .in_3(multiplexer_15_out), .out(multiplexer_12_out));  // open: sel
  Multiplexer #(.Selector_Bits(2), .Bits(8)) multiplexer_13 (
    .sel(multiplexer_14_out), .in_0(A_2_q), .in_1(X_q), .in_2(IP_out), .in_3(AR_q), .out(multiplexer_13_out));
  Multiplexer #(.Bits(2)) multiplexer_14 (.out(multiplexer_14_out));  // open: sel, in_0, in_1
  Register #(.Bits(8)) IR1 (.D(IR0_q), .C(undriven), .en(1'b1), .Q(IR1_q));
  Register #(.Bits(8)) TR (.D(multiplexer_10_out), .C(undriven), .Q(TR_q));  // open: en
  Register #(.Bits(8)) A (.D(multiplexer_11_out), .C(undriven), .Q(A_q));  // open: en
  Register #(.Bits(8)) B (.D(multiplexer_12_out), .C(undriven), .Q(B_q));  // open: en
  Register #(.Bits(8)) IR2 (.D(IR1_q), .C(undriven), .en(1'b1), .Q(IR2_q));
  ROM #(.AddrBits(7), .Bits(8)) upper (.A(multiplexer_13_out[7:1]), .sel(multiplexer_13_out[0]), .D(upper_d));
  not not_2 (not_2_out, multiplexer_13_out[0]);
  RAMDualPort #(.AddrBits(4), .Bits(8)) lower (
    .A(multiplexer_13_out[7:4]), .Din(multiplexer_17_out), .C(undriven), .D(lower_d));  // open: str, ld
  xor xor_1 (xor_1_out[0], B_q[0], undriven_3[7]);
  Multiplexer #(.Bits(8)) multiplexer_15 (.sel(not_2_out), .in_0(upper_d), .in_1(lower_d), .out(multiplexer_15_out));
  assign and_1_out = xor_1_out & A_q;  // And and_1, 8 bits wide
  assign or_5_out = xor_1_out | A_q;  // Or or_5, 8 bits wide
  assign xor_2_out = xor_1_out ^ A_q;  // XOr xor_2, 8 bits wide
  buf or_6 (or_6_out, and_2_out);  // Or open: In_1
  add_and_compare add_and_compare_1 (
    .A(A_q), .B(xor_1_out), .Cin(or_6_out), .S(add_and_compare_1_s), .C(add_and_compare_1_c[1]),
    .O(add_and_compare_1_c[2]), .Z(add_and_compare_1_c[3]));
  Multiplexer #(.Bits(8), .Selector_Bits(2)) multiplexer_16 (
    .in_0(and_1_out), .in_1(or_5_out), .in_2(xor_2_out), .in_3(add_and_compare_1_s), .out(multiplexer_16_out));  // open: sel
  buf and_2 (and_2_out, FR_q[1]);  // And open: In_1
  Register #(.Bits(4)) FR (.D({add_and_compare_1_c, add_and_compare_1_s[0]}), .C(undriven), .Q(FR_q));  // open: en
  Multiplexer #(.Bits(8)) multiplexer_17 (
    .in_0(TR_q), .in_1(multiplexer_16_out), .out(multiplexer_17_out));  // open: sel
  Register #(.Bits(8)) A_2 (.D(multiplexer_17_out), .C(undriven), .Q(A_2_q));  // open: en
  Register #(.Bits(8)) X (.D(multiplexer_17_out), .C(undriven), .Q(X_q));  // open: en
  // Pins of 1 and 8 bits meet at B_q
  // Pins of 1 and 8 bits meet at {8{undriven_3[7]}}
  // Pins of 1 and 8 bits meet at xor_1_out
  // Pins of 1 and 8 bits meet at demultiplexer_2_out_0
  // Pins of 1 and 8 bits meet at demultiplexer_2_out_1
  // Pins of 1 and 8 bits meet at demultiplexer_2_out_2
  // Pins of 1 and 8 bits meet at demultiplexer_2_out_3
  // Pins of 1 and 8 bits meet at {undriven_2, 1'b0}

  // Notes on the sheet:
  //   dout
  //   address
  //   cache (1)
  //   hit
  //   din
  //   stall
  //   ST0
  //   zero
  //   ST1
  //   use ST1 & result instead
  //   of ST2 & A/B if the ALU is
  //   limiting clock speed rather
  //   than memory
  //   ALU
  //   ST2
endmodule
