// Digital circuit memory interface.dig as structural Verilog
module memory_interface (
  input  [15:0] new_address,
  input  clk,
  input  [15:0] old_address,
  input  [7:0] data
);

  wire and_1_out, and_2_out, and_3_out, comparator_1_eq, not_1_out;
  wire [1:0] d_id_out, q_in_out, q_out_out;
  wire [2:0] C0_COMMAND;
  wire [7:0] _64k_d, C0_DATA_OUT, C1_DATA_OUT, C2_DATA_OUT, C3_DATA_OUT, multiplexer_2_out;
  wire [15:0] multiplexer_3_out, multiplexer_4_out;
  wire [17:0] queue_d2;
  wire [18:0] multiplexer_1_out;

  DipSwitch dipswitch_1 (.out(C0_COMMAND[0]));
  DipSwitch dipswitch_2 (.out(C0_COMMAND[1]));
  DipSwitch dipswitch_3 (.out(C0_COMMAND[2]));
  Counter d_id (.en(1'b1), .C(clk), .out(d_id_out[0]));  // open: clr, ovf
  Multiplexer #(.Bits(19), .Selector_Bits(2)) multiplexer_1 (
    .sel(d_id_out), .in_0({new_address, C0_COMMAND}), .in_1({new_address, C0_COMMAND}),
    .in_2({new_address, C0_COMMAND}), .in_3({new_address, C0_COMMAND}), .out(multiplexer_1_out));
  and and_1 (and_1_out, clk, multiplexer_1_out[0]);
  and and_2 (and_2_out, clk, and_3_out);
  Counter #(.Bits(2)) q_in (.en(1'b1), .C(and_1_out), .out(q_in_out));  // open: clr, ovf
  Counter #(.Bits(2)) q_out (.en(1'b1), .C(and_2_out), .out(q_out_out));  // open: clr, ovf
  RAMDualAccess #(.Bits(18)) queue (
    .str(and_1_out), .C(clk), .A1(q_in_out), .Din1(multiplexer_1_out[18:1]), .A2(q_out_out), .D2(queue_d2));  // open: ld, D1
  Comparator #(.Bits(2)) comparator_1 (.a(q_in_out), .b(q_out_out), .eq(comparator_1_eq));  // open: gt, lt
  not not_1 (not_1_out, comparator_1_eq);
  buf and_3 (and_3_out, not_1_out);  // And open: In_1
  Multiplexer #(.Selector_Bits(2), .Bits(8)) multiplexer_2 (
    .sel(queue_d2[1:0]), .in_0(data), .in_1(data), .in_2(data), .in_3(data), .out(multiplexer_2_out));
  Multiplexer #(.Bits(16), .Selector_Bits(2)) multiplexer_3 (
    .sel(queue_d2[1:0]), .in_0(old_address), .in_1(old_address), .in_2(old_address), .in_3(old_address),
    .out(multiplexer_3_out));
  Multiplexer #(.Bits(16)) multiplexer_4 (
    .in_0(multiplexer_3_out), .in_1(queue_d2[17:2]), .out(multiplexer_4_out));  // open: sel
  RAMDualPort #(.AddrBits(16), .Bits(8)) _64k (
    .A(multiplexer_4_out), .Din(multiplexer_2_out), .D(_64k_d));  // open: str, C, ld
  Demultiplexer #(.Bits(8), .Selector_Bits(2)) demultiplexer_1 (
    .sel(queue_d2[1:0]), .in(_64k_d), .out_0(C0_DATA_OUT), .out_1(C1_DATA_OUT), .out_2(C2_DATA_OUT),
    .out_3(C3_DATA_OUT));
  // Pins of 1 and 2 bits meet at d_id_out

  // Other names for the same wires on the sheet: C1_COMMAND[18:0] = {new_address, C0_COMMAND};
  //   C2_COMMAND[18:0] = {new_address, C0_COMMAND}; C3_COMMAND[18:0] = {new_address, C0_COMMAND};
  //   C0_ADDRESS[15:0] = old_address; C1_ADDRESS[15:0] = old_address; C2_ADDRESS[15:0] = old_address;
  //   C3_ADDRESS[15:0] = old_address; C0_DATA_IN[7:0] = data; C1_DATA_IN[7:0] = data; C2_DATA_IN[7:0] = data;
  //   C3_DATA_IN[7:0] = data; clock = clk; C0_COMMAND[18:3] = new_address
endmodule
